# Fritzing sketch connect (saved by Fritzing 1.0.0rc)

parts:
  KY-1 = Keyes Relay [package=THT]
  J1 = 220v plug
  CONN1 = USB connector [package=THT]

nets:
  N1: KY-1.power, CONN1.d-
  N2: KY-1.ground, CONN1.GND, CONN1.chassis5, CONN1.chassis6
  N3: KY-1.NO, J1.pin1

notes:
  ESP32 C3 MINI
  GND VCC GPIO
  220V Output

custom parts:
  Keyes Relay: The Keyes 5V relay module is suitable for SCM development, home appliance control. It uses a 5V~12V TIL control signal which can control DC / AC signal.
  220v plug: Generic 220V AC plug.
